// Logisim project lab_work.circ as structural Verilog: 1 circuit, main circuit main
module main (
  input  S,
  input  O0,
  input  O1,
  input  A0,
  input  A1,
  input  B0,
  input  B1,
  output B,
  output E,
  output L,
  output G,
  output L0,
  output L1,
  output L2,
  output L3,
  output L4,
  output L5,
  output L6,
  output L7,
  output N
);

  wire and_1_out, and_2_out, and_3_out, and_4_out, and_5_out, and_6_out, and_7_out, and_8_out, and_9_out,
       and_10_out, and_11_out, and_12_out, and_13_out, and_14_out, and_15_out, and_16_out, and_17_out,
       and_18_out, and_19_out, and_20_out, and_21_out, and_22_out, and_23_out, and_24_out, and_25_out,
       and_26_out, and_27_out, and_28_out, and_29_out, and_30_out, and_31_out, and_32_out, and_33_out,
       and_34_out, and_35_out, and_36_out, and_37_out, and_38_out, and_39_out, and_40_out, and_41_out,
       and_42_out, and_43_out, and_44_out, and_45_out, and_46_out, and_48_out, and_49_out, and_50_out,
       and_51_out, and_52_out, and_54_out, and_57_out, and_58_out, and_59_out, and_60_out, and_61_out,
       and_62_out, and_64_out, n3_to_8_decoder_74138_1_p5, n3_to_8_decoder_74138_1_p7,
       n3_to_8_decoder_74138_1_p8, n3_to_8_decoder_74138_1_p9, n3_to_8_decoder_74138_1_p10,
       n3_to_8_decoder_74138_1_p11, n3_to_8_decoder_74138_1_p12, n3_to_8_decoder_74138_1_p13,
       n3_to_8_decoder_74138_1_p14, n3_to_8_decoder_74138_2_p5, n3_to_8_decoder_74138_2_p7,
       n3_to_8_decoder_74138_2_p8, n3_to_8_decoder_74138_2_p9, n3_to_8_decoder_74138_2_p10,
       n3_to_8_decoder_74138_3_p3, n3_to_8_decoder_74138_3_p5, n3_to_8_decoder_74138_3_p7,
       n3_to_8_decoder_74138_3_p8, n3_to_8_decoder_74138_3_p9, n3_to_8_decoder_74138_3_p10,
       n3_to_8_decoder_74138_4_p1, n3_to_8_decoder_74138_4_p5, n3_to_8_decoder_74138_4_p7,
       n3_to_8_decoder_74138_4_p8, n3_to_8_decoder_74138_4_p9, n3_to_8_decoder_74138_4_p10,
       n3_to_8_decoder_74138_4_p11, n3_to_8_decoder_74138_4_p12, n3_to_8_decoder_74138_4_p13,
       n3_to_8_decoder_74138_4_p14, n3_to_8_decoder_74138_4_p15, n3_to_8_decoder_74138_4_p16,
       n3_to_8_decoder_74138_4_p17, n3_to_8_decoder_74138_4_p18, not_1_out, not_6_out, not_7_out, not_8_out,
       not_9_out, not_10_out, not_11_out, not_12_out, not_13_out, not_14_out, not_15_out, not_16_out,
       not_17_out, not_18_out, not_19_out, not_20_out, not_21_out, not_22_out, not_25_out, not_27_out,
       not_29_out, not_31_out, not_33_out, not_34_out, not_35_out, not_36_out, not_37_out, or_1_out,
       or_2_out, or_3_out, or_4_out, or_5_out, or_6_out, or_7_out, or_8_out, or_9_out, or_10_out, or_11_out,
       or_12_out, or_13_out, or_14_out, or_15_out, or_16_out, or_17_out, or_18_out, or_19_out, or_20_out,
       or_21_out, or_22_out, or_23_out, or_24_out, or_25_out, or_26_out, or_27_out, or_28_out, or_29_out,
       or_30_out, or_31_out, or_32_out, or_33_out, or_34_out, or_35_out, or_36_out, or_37_out;

  not not_1 (not_1_out, 1'b1);
  // _3_to_8_decoder__74138 #(.Facing("east")) 3_to_8_decoder_74138_1: pin names not known; wires that end beside it: S, O0, O1, 1'b1, n3_to_8_decoder_74138_1_p5, n3_to_8_decoder_74138_1_p5, n3_to_8_decoder_74138_1_p7, n3_to_8_decoder_74138_1_p8, n3_to_8_decoder_74138_1_p9, n3_to_8_decoder_74138_1_p10, n3_to_8_decoder_74138_1_p11, n3_to_8_decoder_74138_1_p12, n3_to_8_decoder_74138_1_p13, n3_to_8_decoder_74138_1_p14
  not not_2 (n3_to_8_decoder_74138_1_p5, 1'b1);
  // _3_to_8_decoder__74138 #(.Facing("east")) 3_to_8_decoder_74138_2: pin names not known; wires that end beside it: A0, A1, not_1_out, 1'b1, n3_to_8_decoder_74138_2_p5, n3_to_8_decoder_74138_2_p5, n3_to_8_decoder_74138_2_p7, n3_to_8_decoder_74138_2_p8, n3_to_8_decoder_74138_2_p9, n3_to_8_decoder_74138_2_p10
  not not_3 (n3_to_8_decoder_74138_2_p5, 1'b1);
  // _3_to_8_decoder__74138 #(.Facing("east")) 3_to_8_decoder_74138_3: pin names not known; wires that end beside it: B0, B1, n3_to_8_decoder_74138_3_p3, 1'b1, n3_to_8_decoder_74138_3_p5, n3_to_8_decoder_74138_3_p5, n3_to_8_decoder_74138_3_p7, n3_to_8_decoder_74138_3_p8, n3_to_8_decoder_74138_3_p9, n3_to_8_decoder_74138_3_p10
  not not_4 (n3_to_8_decoder_74138_3_p3, 1'b1);
  not not_5 (n3_to_8_decoder_74138_3_p5, 1'b1);
  not not_6 (not_6_out, n3_to_8_decoder_74138_1_p7);
  not not_7 (not_7_out, n3_to_8_decoder_74138_1_p8);
  not not_8 (not_8_out, n3_to_8_decoder_74138_1_p9);
  not not_9 (not_9_out, n3_to_8_decoder_74138_1_p10);
  not not_10 (not_10_out, n3_to_8_decoder_74138_1_p11);
  not not_11 (not_11_out, n3_to_8_decoder_74138_1_p12);
  not not_12 (not_12_out, n3_to_8_decoder_74138_1_p13);
  not not_13 (not_13_out, n3_to_8_decoder_74138_1_p14);
  not not_14 (not_14_out, n3_to_8_decoder_74138_2_p7);
  not not_15 (not_15_out, n3_to_8_decoder_74138_2_p8);
  not not_16 (not_16_out, n3_to_8_decoder_74138_2_p9);
  not not_17 (not_17_out, n3_to_8_decoder_74138_2_p10);
  not not_18 (not_18_out, n3_to_8_decoder_74138_3_p7);
  not not_19 (not_19_out, n3_to_8_decoder_74138_3_p8);
  not not_20 (not_20_out, n3_to_8_decoder_74138_3_p9);
  not not_21 (not_21_out, n3_to_8_decoder_74138_3_p10);
  or or_1 (or_1_out, not_6_out, not_7_out);
  or or_2 (or_2_out, not_8_out, not_9_out);
  not not_22 (not_22_out, B0);
  and and_1 (and_1_out, not_14_out, not_19_out);
  and and_2 (and_2_out, not_15_out, not_18_out);
  and and_3 (and_3_out, not_16_out, not_18_out);
  and and_4 (and_4_out, not_15_out, not_19_out);
  and and_5 (and_5_out, not_14_out, not_20_out);
  and and_6 (and_6_out, not_14_out, not_21_out);
  and and_7 (and_7_out, not_15_out, not_20_out);
  and and_8 (and_8_out, not_16_out, not_19_out);
  and and_9 (and_9_out, not_17_out, not_18_out);
  and and_10 (and_10_out, not_15_out, not_21_out);
  and and_11 (and_11_out, not_16_out, not_20_out);
  and and_12 (and_12_out, not_17_out, not_19_out);
  and and_13 (and_13_out, not_17_out, not_20_out);
  and and_14 (and_14_out, not_21_out, not_16_out);
  and and_15 (and_15_out, not_17_out, not_21_out);
  and and_16 (and_16_out, not_14_out, not_18_out);
  and and_17 (and_17_out, not_15_out, not_19_out);
  and and_18 (and_18_out, not_16_out, not_20_out);
  and and_19 (and_19_out, not_17_out, not_21_out);
  and and_20 (and_20_out, not_14_out, not_19_out);
  and and_21 (and_21_out, not_15_out, not_18_out);
  and and_22 (and_22_out, not_15_out, not_20_out);
  and and_23 (and_23_out, not_16_out, not_19_out);
  and and_24 (and_24_out, not_17_out, not_20_out);
  and and_25 (and_25_out, not_16_out, not_21_out);
  and and_26 (and_26_out, not_14_out, not_20_out);
  and and_27 (and_27_out, not_16_out, not_18_out);
  and and_28 (and_28_out, not_15_out, not_21_out);
  and and_29 (and_29_out, not_17_out, not_19_out);
  and and_30 (and_30_out, not_14_out, not_21_out);
  and and_31 (and_31_out, not_17_out, not_18_out);
  or or_3 (or_3_out, and_1_out, and_2_out);
  or or_4 (or_4_out, and_3_out, and_4_out);
  or or_5 (or_5_out, or_4_out, and_5_out);
  or or_6 (or_6_out, and_6_out, and_7_out);
  or or_7 (or_7_out, or_6_out, or_8_out);
  or or_8 (or_8_out, and_8_out, and_9_out);
  or or_9 (or_9_out, and_10_out, and_11_out);
  or or_10 (or_10_out, and_13_out, and_14_out);
  or or_11 (or_11_out, and_16_out, and_17_out);
  or or_12 (or_12_out, or_11_out, or_13_out);
  or or_13 (or_13_out, and_18_out, and_19_out);
  or or_14 (or_14_out, and_20_out, and_21_out);
  or or_15 (or_15_out, or_14_out, or_16_out);
  or or_16 (or_16_out, and_22_out, and_23_out);
  or or_17 (or_17_out, and_24_out, and_25_out);
  or or_18 (or_18_out, and_26_out, and_27_out);
  or or_19 (or_19_out, or_18_out, or_20_out);
  or or_20 (or_20_out, and_28_out, and_29_out);
  or or_21 (or_21_out, and_30_out, and_31_out);
  and and_32 (and_32_out, not_14_out, not_18_out);
  and and_33 (and_33_out, not_15_out, not_19_out);
  and and_34 (and_34_out, not_16_out, not_20_out);
  and and_35 (and_35_out, not_17_out, not_21_out);
  and and_36 (and_36_out, not_17_out, not_18_out);
  and and_37 (and_37_out, not_17_out, not_19_out);
  and and_38 (and_38_out, not_17_out, not_20_out);
  and and_39 (and_39_out, not_16_out, not_18_out);
  and and_40 (and_40_out, not_16_out, not_19_out);
  and and_41 (and_41_out, not_15_out, not_18_out);
  or or_22 (or_22_out, not_16_out, not_17_out);
  and and_42 (and_42_out, not_12_out, 1'b1);
  and and_43 (and_43_out, and_42_out, or_3_out);
  and and_44 (and_44_out, and_42_out, or_5_out);
  and and_45 (and_45_out, and_42_out, or_7_out);
  and and_46 (and_46_out, and_42_out, or_23_out);
  or or_23 (or_23_out, or_9_out, and_12_out);
  and and_47 (L5, and_42_out, or_10_out);
  and and_48 (and_48_out, and_42_out, and_15_out);
  or or_24 (or_24_out, or_15_out, or_17_out);
  and and_49 (and_49_out, B0, A1);
  and and_50 (and_50_out, A0, not_22_out);
  or or_25 (or_25_out, and_32_out, and_33_out);
  or or_26 (or_26_out, and_34_out, and_35_out);
  or or_27 (or_27_out, and_36_out, and_37_out);
  or or_28 (or_28_out, and_39_out, and_40_out);
  and and_51 (and_51_out, or_22_out, not_10_out);
  // _3_to_8_decoder__74138 #(.Facing("east")) 3_to_8_decoder_74138_4: pin names not known; wires that end beside it: n3_to_8_decoder_74138_4_p1, A0, A1, not_11_out, n3_to_8_decoder_74138_4_p5, n3_to_8_decoder_74138_4_p5, n3_to_8_decoder_74138_4_p7, n3_to_8_decoder_74138_4_p8, n3_to_8_decoder_74138_4_p9, n3_to_8_decoder_74138_4_p10, n3_to_8_decoder_74138_4_p11, n3_to_8_decoder_74138_4_p12, n3_to_8_decoder_74138_4_p13, n3_to_8_decoder_74138_4_p14, n3_to_8_decoder_74138_4_p15, n3_to_8_decoder_74138_4_p16, n3_to_8_decoder_74138_4_p17, n3_to_8_decoder_74138_4_p18
  not not_23 (n3_to_8_decoder_74138_4_p1, 1'b1);
  and and_52 (and_52_out, not_14_out, not_18_out);
  or or_29 (or_29_out, and_49_out, and_50_out);
  and and_53 (E, or_1_out, or_30_out);
  or or_30 (or_30_out, or_25_out, or_26_out);
  or or_31 (or_31_out, or_27_out, and_38_out);
  not not_24 (n3_to_8_decoder_74138_4_p5, 1'b1);
  and and_54 (and_54_out, and_42_out, and_52_out);
  or or_32 (or_32_out, or_31_out, or_33_out);
  or or_33 (or_33_out, or_28_out, and_41_out);
  not not_25 (not_25_out, n3_to_8_decoder_74138_4_p7);
  not not_26 (n3_to_8_decoder_74138_4_p15, n3_to_8_decoder_74138_4_p8);
  not not_27 (not_27_out, n3_to_8_decoder_74138_4_p9);
  not not_28 (n3_to_8_decoder_74138_4_p16, n3_to_8_decoder_74138_4_p10);
  not not_29 (not_29_out, n3_to_8_decoder_74138_4_p11);
  not not_30 (n3_to_8_decoder_74138_4_p17, n3_to_8_decoder_74138_4_p12);
  not not_31 (not_31_out, n3_to_8_decoder_74138_4_p13);
  not not_32 (n3_to_8_decoder_74138_4_p18, n3_to_8_decoder_74138_4_p14);
  and and_55 (B, or_2_out, or_29_out);
  not not_33 (not_33_out, E);
  and and_56 (G, or_1_out, or_32_out);
  not not_34 (not_34_out, or_32_out);
  and and_57 (and_57_out, not_33_out, not_35_out);
  not not_35 (not_35_out, G);
  not not_36 (not_36_out, and_51_out);
  not not_37 (not_37_out, or_30_out);
  and and_58 (and_58_out, not_34_out, not_13_out);
  and and_59 (and_59_out, not_13_out, or_12_out);
  and and_60 (and_60_out, not_13_out, or_24_out);
  and and_61 (and_61_out, not_13_out, or_19_out);
  and and_62 (and_62_out, not_13_out, or_21_out);
  and and_63 (L, and_57_out, or_1_out);
  or or_34 (or_34_out, not_25_out, and_64_out);
  and and_64 (and_64_out, not_36_out, not_10_out);
  or or_35 (or_35_out, and_51_out, and_43_out);
  or or_36 (or_36_out, not_27_out, and_44_out);
  and and_65 (N, not_37_out, and_58_out);
  or or_37 (or_37_out, or_34_out, and_54_out);
  or or_38 (L4, not_29_out, and_46_out);
  or or_39 (L6, not_31_out, and_48_out);
  or or_40 (L0, or_37_out, and_59_out);
  or or_41 (L1, and_60_out, or_35_out);
  or or_42 (L2, or_36_out, and_61_out);
  or or_43 (L3, and_45_out, and_62_out);
  not not_38 (L7, 1'b1);
endmodule
